# Fritzing sketch Sketch (saved by Fritzing 0.9.3b)
breadboards: 1

parts:
  Componente1 = Arduino Uno (Rev3)
  LED1 = smd LED [color="Red (633nm)" package="0805 [SMD]"]
  U1 = POT [package=pot_alpha_rv16af-20]
  LED2 = LEDs [package=led10mm]
  LED3 = LEDs [package=led10mm]
  LED4 = LEDs [package=led10mm]
  S1 = Pushbutton [package="[SMD]"]
  S2 = Pushbutton [package="[SMD]"]
  S3 = Pushbutton [package="[SMD]"]
  S4 = Pushbutton [package="[SMD]"]
  R1 = Resistor [tolerance=±5% resistance=220 package="2010 [SMD]"]
  R2 = Resistor [tolerance=±5% resistance=220 package="2010 [SMD]"]
  R3 = Resistor [tolerance=±5% resistance=220 package="2010 [SMD]"]
  R4 = Resistor [tolerance=±5% resistance=220 package="2010 [SMD]"]
  R5 = Resistor [tolerance=±5% resistance=220 package="2010 [SMD]"]
  R6 = Resistor [tolerance=±5% resistance=220 package="2010 [SMD]"]
  R10 = Resistor [tolerance=±5% resistance=220 package="2010 [SMD]"]
  R11 = Resistor [tolerance=±5% resistance=220 package="2010 [SMD]"]
  R12 = Resistor [tolerance=±5% resistance=220 package="2010 [SMD]"]
  LED5 = LEDs [package=led10mm]

nets:
  N1: Componente1.A0, U1.S
  N2: Componente1.D8, S4.Pin_3, S4.Pin_4, R12.Pin_1
  N3: Componente1.D9_PWM, S3.Pin_3, S3.Pin_4, R11.Pin_1
  N4: Componente1.D10_PWM/SS, S2.Pin_3, S2.Pin_4, R10.Pin_1
  N5: Componente1.D11_PWM/MOSI, S1.Pin_3, S1.Pin_4, R6.Pin_1
  N6: Componente1.D0/RX, LED1.anode
  N7: Componente1.D1/TX, LED5.A
  N8: Componente1.D2, LED4.A
  N9: Componente1.D3_PWM, LED3.A
  N10: Componente1.D4, LED2.A
  N11: Componente1.5V, U1.E
  N12: Componente1.GND, U1.A, R1.Pin_0, R2.Pin_0, R3.Pin_0, R4.Pin_0, R5.Pin_0, R6.Pin_0, R10.Pin_0, R11.Pin_0, R12.Pin_0
  N13: LED1.cathode, R1.Pin_1
  N14: LED2.C, R2.Pin_1
  N15: LED3.C, R3.Pin_1
  N16: LED4.C, R4.Pin_1
  N17: S1.Pin_1, S1.Pin_2
  N18: S2.Pin_1, S2.Pin_2
  N19: S3.Pin_1, S3.Pin_2
  N20: S4.Pin_1, S4.Pin_2
  N21: R5.Pin_1, LED5.C
